# Fritzing sketch arduinoUno_project1 (saved by Fritzing 0.9.10b)
breadboards: 1

parts:
  S1 = Pushbutton [package="[THT]"]
  Part1 = Arduino Uno (Rev3)
  J1 = Basic Servo
  ZS-042_RTC1 = ZS-042 RTC Module
  LED2 = RGB LED - (4 legs) [package="5 mm [THT]"]
  HC-SR04_Sensor_1 = HC-SR04 Ultrasonic Distance Sensor
  R1 = Resistor [tolerance=±5% power=0.25 resistance=220 package=THT]
  R2 = Resistor [tolerance=±5% power=0.25 resistance=220 package=THT]
  R3 = Resistor [tolerance=±5% power=0.25 resistance=220 package=THT]

nets:
  GND: S1.Pin_1, S1.Pin_2, Part1.GND, J1.gnd, ZS-042_RTC1.GND, LED2.common_anode, HC-SR04_Sensor_1.GND
  N1: S1.Pin_3, S1.Pin_4, Part1.D2
  N2: Part1.D8, J1.pulse
  N3: Part1.A4/SDA, ZS-042_RTC1.SDA
  N4: Part1.A5/SCL, ZS-042_RTC1.SCL
  N5: Part1.D3_PWM, R2.Pin_1
  N6: Part1.D4, R1.Pin_1
  N7: Part1.D5_PWM, R3.Pin_1
  N8: Part1.D6_PWM, HC-SR04_Sensor_1.TRIG
  N9: Part1.D7, HC-SR04_Sensor_1.ECHO
  VCC: Part1.3V3, J1.vcc, HC-SR04_Sensor_1.VCC
  5V: Part1.5V, ZS-042_RTC1.VCC
  N10: LED2.red_cathode, R2.Pin_0
  N11: LED2.green_cathode, R1.Pin_0
  N12: LED2.blue_cathode, R3.Pin_0
