# Fritzing sketch Gr10-092-160-Project2-Fritzing (saved by Fritzing 0.9.10b)
breadboards: 1

parts:
  J1 = Basic Servo
  Mod1 = Amica NodeMCU DEVKIT 1.0
  HC-SR04_Sensor_1 = HC-SR04 Ultrasonic Distance Sensor
  R1 = Resistor [tolerance=±5% power=0.25 resistance=220 package=THT]
  S1 = Pushbutton [package="[THT]"]
  R2 = Resistor [tolerance=±5% power=0.25 resistance=220 package=THT]
  R3 = Resistor [tolerance=±5% power=0.25 resistance=220 package=THT]
  LED1 = RGB LED - (4 legs) [package="5 mm [THT]"]
  ZS-042_RTC1 = ZS-042 RTC Module

nets:
  GND: J1.gnd, Mod1.pin2, HC-SR04_Sensor_1.GND, S1.Pin_1, S1.Pin_2, LED1.common_anode, ZS-042_RTC1.GND
  VCC: J1.vcc, Mod1.pin1, Mod1.pin_10, HC-SR04_Sensor_1.VCC, ZS-042_RTC1.VCC
  N1: Mod1.pin5, S1.Pin_3, S1.Pin_4
  N2: Mod1.pin_16, HC-SR04_Sensor_1.TRIG
  N3: Mod1.pin_17, HC-SR04_Sensor_1.ECHO
  N4: Mod1.pin_18, R1.Pin_1
  N5: Mod1.pin_19, R2.Pin_1
  N6: Mod1.pin_21, ZS-042_RTC1.SDA
  N7: Mod1.pin_22, ZS-042_RTC1.SCL
  N8: Mod1.pin_23, R3.Pin_1
  N9: R1.Pin_0, LED1.red_cathode
  N10: R2.Pin_0, LED1.green_cathode
  N11: R3.Pin_0, LED1.blue_cathode
