# Fritzing sketch ESP32_LED_PushButton (saved by Fritzing 0.9.10b)
breadboards: 1

parts:
  R1 = Resistor [tolerance=±5% resistance=220 package="0402 [SMD]"]
  U1 = ESP32-38PinWide [part_number=ESP32-38PinWide]
  LED1 = LED - 5mm [color="Red (633nm)" current=0.030 package="5 mm [THT]"]
  S1 = Pushbutton [package="[SMD]"]

nets:
  N1: R1.Pin_0, LED1.anode
  N2: R1.Pin_1, U1.GPIO18
  N3: U1.GPIO16, S1.Pin_3, S1.Pin_4
  N4: U1.GND, LED1.cathode, S1.Pin_1, S1.Pin_2

notes:
  a. LED anode -> 220 kΩ -> GPIO 18
  b. LED cathode -> GND
  c. Push button one pin -> GPIO 14
  d. Push button another pin -> GND

custom parts:
  ESP32-38PinWide: Generic 38-Pin ESP32 with wide format (only access to one side of pins on a breadboard) based on Stephen Lilley's HiLetgo ESP-WROOM-32 ESP32 ESP-32S Development Board.
