# Fritzing sketch ESP32_RGB_LED_PWM (saved by Fritzing 0.9.10b)
breadboards: 1

parts:
  ESP32 = ESP32-38PinWide [part_number=ESP32-38PinWide]
  LED1 = RGB LED (com. cathode, rgb) [package="5 mm [THT]"]
  R1 = Resistor [tolerance=±5% resistance=220 package="2010 [SMD]"]
  R2 = Resistor [tolerance=±5% resistance=220 package="2010 [SMD]"]
  R3 = Resistor [tolerance=±5% resistance=220 package="2010 [SMD]"]
  U1 = POT [knob_status=50% power=0.5W package=3362u]

nets:
  N1: ESP32.3.3, U1.E
  N2: ESP32.GPIO33, U1.S
  N3: ESP32.GND, LED1.common_cathode, U1.A
  N4: ESP32.GPIO21, R3.Pin_1
  N5: ESP32.GPIO22, R2.Pin_1
  N6: ESP32.GPIO23, R1.Pin_1
  N7: LED1.red_anode, R1.Pin_0
  N8: LED1.green_anode, R2.Pin_0
  N9: LED1.blue_anode, R3.Pin_0

notes:
  RGB-LED Red -> GPIO25
  RGB-LED Green -> GPIO26
  RGB-LED Blue -> GPIO27
  RGB-LED Common Catode -> GND
  if RGB-LED Common Anode -> 3.3V
  POT Pin 1 -> 3.3V
  POT Pin 2 -> GPIO 33
  POT Pin 3 -> GND

custom parts:
  ESP32-38PinWide: Generic 38-Pin ESP32 with wide format (only access to one side of pins on a breadboard) based on Stephen Lilley's HiLetgo ESP-WROOM-32 ESP32 ESP-32S Development Board.
