# Fritzing sketch ESP32_Servo (saved by Fritzing 0.9.10b)
breadboards: 1

parts:
  M1 = Dagu DGServo 9g (Pan and tilt) [part_number=RS001B]
  U1 = ESP32-38PinWide [part_number=ESP32-38PinWide]

nets:
  N1: M1.gnd, U1.GPIO23
  N2: M1.vcc, U1.3.3
  N3: M1.pulse, U1.GND

custom parts:
  ESP32-38PinWide: Generic 38-Pin ESP32 with wide format (only access to one side of pins on a breadboard) based on Stephen Lilley's HiLetgo ESP-WROOM-32 ESP32 ESP-32S Development Board.
