# Fritzing sketch ESP32_Microphone_I2S (saved by Fritzing 0.9.10b)
breadboards: 1

parts:
  Part1 = INMP441
  U1 = ESP32-38PinWide [part_number=ESP32-38PinWide]

nets:
  N1: Part1.L/R, U1.GPIO14
  N2: Part1.WS, U1.GPIO12
  N3: Part1.SD, U1.GPIO13
  N4: Part1.VDD, U1.3.3
  GND: Part1.GND, U1.GND

custom parts:
  INMP441: This is a simple breakout board for the INMP441 I2S MEMS microphone.
  ESP32-38PinWide: Generic 38-Pin ESP32 with wide format (only access to one side of pins on a breadboard) based on Stephen Lilley's HiLetgo ESP-WROOM-32 ESP32 ESP-32S Development Board.
