# Fritzing sketch PartA_AHT20_with_I2C (saved by Fritzing 0.9.9b)
breadboards: 1

parts:
  Part1 = Adafruit AHT20 Temperature and Humidity Sensor [part_number="Adafruit #4566"]
  U1 = ESP32-38PinWide [part_number=ESP32-38PinWide]

nets:
  N1: Part1.VCC, U1.3.3
  GND: Part1.GND, U1.GND
  N2: Part1.SCL, U1.GPIO22
  N3: Part1.SDA, U1.GPIO21

notes:
  ESP32_AHT0

custom parts:
  Adafruit AHT20 Temperature and Humidity Sensor: The AHT20 is a nice but inexpensive temperature and humidity sensor from the same folks that brought us the DHT22. You can take sensor readings as often as you like, and it uses standard I2C so its super easy to use with any Arduino or Linux/Raspberry Pi board. This sensor has a typical accuracy of +- 2% relative humidity, and +-0.3 °C. There is only one I2C address so its not a good option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
  ESP32-38PinWide: Generic 38-Pin ESP32 with wide format (only access to one side of pins on a breadboard) based on Stephen Lilley's HiLetgo ESP-WROOM-32 ESP32 ESP-32S Development Board.

// code stored in the sketch: AHT20_ESP32_20220518.bas
//AHT20 Temperature sensor demo done on 01/03/2022
//Ref: http://www.esp32learning.com/code/aht20-integrated-temperature-and-humidity-sensor-and-esp32-board-example.php
//Ref for AHT20 Fritzing: https://github.com/adafruit/Fritzing-Library/blob/master/parts/Adafruit%20AHT20%20Temperature%20and%20Humidity%20Sensor.fzpz
#include <Adafruit_AHTX0.h>
 
Adafruit_AHTX0 aht;
 
void setup() 
{
  Serial.begin(115200);
  Serial.println("Adafruit AHT10/AHT20 demo!");
  Serial.println("AHT20 Temperature sensor demo done on 01/03/2022");
  Serial.println("Ref: http://www.esp32learning.com/code/aht20-integrated-temperature-and-humidity-sensor-and-esp32-board-example.php");
 
  if (! aht.begin()) 
  {
    Serial.println("Could not find AHT? Check wiring");
    while (1) delay(10);
  }
  Serial.println("AHT10 or AHT20 found");
}
 
void loop() {
  sensors_event_t humidity, temp;
  aht.getEvent(&humidity, &temp);// populate temp and humidity objects with fresh data
  Serial.print("Temperature: "); 
  Serial.print(temp.temperature); 
  Serial.println(" degrees C");
  Serial.print("Humidity: "); 
  Serial.print(humidity.relative_humidity); 
  Serial.println("% rH");
 
  delay(500);
}
