# Fritzing sketch ESP32_HC-SR04P_Ultrasonic_Distance_Sensor_CircuitDiagram (saved by Fritzing 0.9.10b)
breadboards: 1

parts:
  HC-SR04_Sensor_1 = HC-SR04 Ultrasonic Distance Sensor
  U1 = ESP32-38PinWide [part_number=ESP32-38PinWide]

nets:
  VCC: HC-SR04_Sensor_1.VCC, U1.VIN
  N1: HC-SR04_Sensor_1.TRIG, U1.GPIO23
  N2: HC-SR04_Sensor_1.ECHO, U1.GPIO22
  GND: HC-SR04_Sensor_1.GND, U1.GND

notes:
  Trig -> GPIO23
  Echo -> GPIO22
  VCC -> Vin
  GND -> GND

custom parts:
  ESP32-38PinWide: Generic 38-Pin ESP32 with wide format (only access to one side of pins on a breadboard) based on Stephen Lilley's HiLetgo ESP-WROOM-32 ESP32 ESP-32S Development Board.
