# Fritzing sketch ESP32_FSM_CircuitDiagram (saved by Fritzing 0.9.10b)
breadboards: 1

parts:
  U1 = ESP32-38PinWide [part_number=ESP32-38PinWide]
  LED1 = LED - 3mm [color="Red (633nm)" current=0.030 package="3 mm [THT]"]
  LED2 = LED - 3mm [color="Green (560nm)" current=0.030 package="3 mm [THT]"]
  R1 = Resistor [tolerance=±5% resistance=220 package="0603 [SMD]"]
  R2 = Resistor [tolerance=±5% resistance=220 package="0603 [SMD]"]
  S1 = Momentary Switch [package=ksa_sealed_tac_switch]
  S2 = Momentary Switch [package=ksa_sealed_tac_switch]

nets:
  N1: U1.GPIO14, S2.2
  N2: U1.GPIO13, S1.2
  N3: U1.GPIO2, R2.Pin_1
  N4: U1.GPIO4, R1.Pin_1
  N5: U1.GND, LED1.cathode, LED2.cathode, S1.4, S2.4
  N6: LED1.anode, R1.Pin_0
  N7: LED2.anode, R2.Pin_0

notes:
  1st LED -> GPIO4
  2nd LED ->GPIO2
  1st Push button -> GPIO13
  2nd Push button -> GPIO14

custom parts:
  ESP32-38PinWide: Generic 38-Pin ESP32 with wide format (only access to one side of pins on a breadboard) based on Stephen Lilley's HiLetgo ESP-WROOM-32 ESP32 ESP-32S Development Board.
