# Fritzing sketch ESP32_PID_CircuitDiagram (saved by Fritzing 0.9.10b)
breadboards: 1

parts:
  U1 = ESP32-38PinWide [part_number=ESP32-38PinWide]
  LED1 = LED - 3mm [color="Red (633nm)" current=0.030 package="3 mm [THT]"]
  R1 = Resistor [tolerance=±5% resistance=220 package="0603 [SMD]"]
  U2 = POT [knob_status=50% power=0.5W package=3362u]
  R2 = Photocell (LDR) [package=THT]
  R3 = Resistor [tolerance=±5% resistance=1k package="0603 [SMD]"]

nets:
  N1: U1.3.3, U2.E, R3.Pin_1
  N2: U1.GPIO34, U2.S
  N3: U1.GPIO32, R1.Pin_1
  N4: U1.GPIO33, R2.pin_1, R3.Pin_0
  N5: U1.GND, LED1.cathode, U2.A
  N6: LED1.anode, R1.Pin_0

notes:
  220 Ohms
  1k Ohms
  LED -> 220 Ohms -> GPIO32
  POT pin 2 -> GPIO34
  LDR -> GPIO33 ->1k Ohms ->3.3V

custom parts:
  ESP32-38PinWide: Generic 38-Pin ESP32 with wide format (only access to one side of pins on a breadboard) based on Stephen Lilley's HiLetgo ESP-WROOM-32 ESP32 ESP-32S Development Board.
